// Digital circuit alu.dig as structural Verilog
module alu (
  input  [7:0] REGA,
  input  [7:0] REGB,
  input  ALUE,
  output [7:0] OUT
);

  wire _74283_1_p12, _74283_1_p13, _74283_1_p14, _74283_1_p15, _74283_1_p16, _74283_2_p12, _74283_2_p13,
       _74283_2_p14, _74283_2_p15;

  // _74283 _74283_1: pin names not known; wires that end beside it: 1'b0, REGA[0], REGA[1], REGA[2], REGA[3], REGB[0], REGB[1], REGB[2], REGB[3], 1'b1, 1'b0, _74283_1_p12, _74283_1_p13, _74283_1_p14, _74283_1_p15, _74283_1_p16
  // _74283 _74283_2: pin names not known; wires that end beside it: _74283_1_p16, REGA[4], REGA[5], REGA[6], REGA[7], REGB[4], REGB[5], REGB[6], REGB[7], 1'b1, 1'b0, _74283_2_p12, _74283_2_p13, _74283_2_p14, _74283_2_p15, 1'b0
  _74245 _74245_1 (
    .pin1(1'b1), .pin2(_74283_1_p12), .pin3(_74283_1_p13), .pin4(_74283_1_p14), .pin5(_74283_1_p15),
    .pin6(_74283_2_p12), .pin7(_74283_2_p13), .pin8(_74283_2_p14), .pin9(_74283_2_p15), .pin10(1'b0),
    .pin11(OUT[7]), .pin12(OUT[6]), .pin13(OUT[5]), .pin14(OUT[4]), .pin15(OUT[3]), .pin16(OUT[2]),
    .pin17(OUT[1]), .pin18(OUT[0]), .pin19(ALUE), .pin20(1'b1));
endmodule
