// Digital circuit computer.dig as structural Verilog
module computer (
  input  [7:0] in_1,
  input  in_3,
  input  in_5,
  input  clk,
  input  [3:0] in_11,
  output [7:0] out_2,
  output [7:0] out_4,
  output [15:0] MCCMD,
  output [7:0] vcx,
  output [7:0] out_8,
  output [3:0] INSTR
);

  wire not_1_out, not_2_out, not_3_out, not_4_out;
  wire [3:0] mccount_1_num, MEMADDR_out;
  wire [7:4] MEMADDR_out_2;

  not not_1 (not_1_out, clk);
  mccount mccount_1 (.CLK(not_1_out), .NUM(mccount_1_num));
  not not_2 (not_2_out, MCCMD[4]);
  not not_3 (not_3_out, MCCMD[5]);
  registerr MEMADDR (
    .CLK(clk), .INP(out_2), .SET(MCCMD[6]), .RST(1'b0), .GET(MCCMD[7]), .OUT({MEMADDR_out_2, MEMADDR_out}),
    .VAL(out_8));
  not not_4 (not_4_out, MCCMD[12]);
  RAMSinglePort #(.AddrBits(4), .isProgramMemory("true"), .Bits(8)) ramsingleport_1 (
    .A(MEMADDR_out), .str(not_2_out), .C(clk), .ld(not_3_out), .D(out_2));
  instreg u_INSTR (
    .IRO(MCCMD[9]), .INP(out_2), .CLK(clk), .IRI(MCCMD[8]), .CLR(not_4_out), .INSTR(in_11), .OUT(out_2),
    .VAL(vcx));
  EEPROM #(.AddrBits(8), .Bits(16)) eeprom_1 (.A({in_11, mccount_1_num}), .CS(1'b1), .WE(1'b0), .OE(1'b1), .D(MCCMD));
  assign out_2 = in_3 ? in_1 : 8'bz;  // Driver driver_1
  register REGA (.CLK(clk), .INP(out_2), .SET(MCCMD[0]), .GET(MCCMD[1]), .OUT(out_2));
  register REGB (.CLK(clk), .INP(out_2), .SET(MCCMD[2]), .GET(MCCMD[3]), .OUT(out_2));
  pc pc_1 (.CLK(clk), .CLR(in_5), .INCR(MCCMD[11]), .PO(MCCMD[10]), .COUNTER(out_2));

  assign INSTR = in_11;
  assign out_4 = out_2;
  // also tied to GND on the sheet: {MEMADDR_out_2[4], MEMADDR_out_2[5], MEMADDR_out_2[6], MEMADDR_out_2[7]}

  // Other names for the same wires on the sheet: AI = MCCMD[0]; AO = MCCMD[1]; BI = MCCMD[2]; BO = MCCMD[3];
  //   MEMI = MCCMD[4]; MEMO = MCCMD[5]; MAI = MCCMD[6]; MAO = MCCMD[7]; IRI = MCCMD[8]; IRO = MCCMD[9];
  //   PO = MCCMD[10]; PINCR = MCCMD[11]; IRCLR = MCCMD[12]

  // Notes on the sheet:
  //   contents of eeprom_1 (hex, n*v repeats v):
  //   fbbf,ffff,ffff,ffff,ffff,f65f,0,0,0,0,0,0,0,0,0,0,fdbf,ff5f,ffff,ffff,ffff,efff,0,
  //   0,0,0,0,0,0,0,0,0,fffd,0,0,0,0,efff
endmodule
