// Digital circuit counter.dig as structural Verilog
module counter (
  input  CLK,
  input  CLR,
  output [3:0] OUT
);

  wire _7476_1_pin10, _7476_1_pin14, _7476_2_pin10, _7476_2_pin14;

  _7476 _7476_1 (
    .pin1(CLK), .pin2(1'b1), .pin3(CLR), .pin4(1'b1), .pin5(1'b1), .pin6(OUT[0]), .pin7(1'b1), .pin8(CLR),
    .pin9(1'b1), .pin10(_7476_1_pin10), .pin11(OUT[1]), .pin12(1'b1), .pin13(1'b0), .pin14(_7476_1_pin14),
    .pin15(OUT[0]), .pin16(1'b1));
  _7476 _7476_2 (
    .pin1(OUT[1]), .pin2(1'b1), .pin3(CLR), .pin4(1'b1), .pin5(1'b1), .pin6(OUT[2]), .pin7(1'b1), .pin8(CLR),
    .pin9(1'b1), .pin10(_7476_2_pin10), .pin11(OUT[3]), .pin12(1'b1), .pin13(1'b0), .pin14(_7476_2_pin14),
    .pin15(OUT[2]), .pin16(1'b1));
  LED led_1 (.in(_7476_1_pin14));
  LED led_2 (.in(_7476_1_pin10));
  LED led_3 (.in(_7476_2_pin14));
  LED led_4 (.in(_7476_2_pin10));

  // Notes on the sheet:
  //   CLR: default 1
endmodule

/* Test case:
CLK CLR OUT
Z   Z   X
0   0   0
C   1   1
C   1   2
*/
