// Digital circuit digital.dig as structural Verilog
module digital (
  input  a,
  input  b,
  output out_3,
  output out_4
);

  nor nor_1 (out_3, a, out_4);
  nor nor_2 (out_4, out_3, b);
endmodule
