// Digital circuit instreg.dig as structural Verilog
module instreg (
  input  IRO,
  input  [7:0] INP,
  input  CLK,
  input  IRI,
  input  CLR,
  output [3:0] INSTR,
  output [7:0] OUT,
  output [7:0] VAL
);

  wire [3:0] registerr_1_out;

  registerr registerr_1 (
    .CLK(CLK), .INP(INP), .SET(IRI), .RST(CLR), .GET(1'b0), .OUT({INSTR, registerr_1_out}), .VAL(VAL));
  _74245 _74245_1 (
    .pin1(1'b1), .pin2(registerr_1_out[0]), .pin3(registerr_1_out[1]), .pin4(registerr_1_out[2]),
    .pin5(registerr_1_out[3]), .pin6(1'b0), .pin7(1'b0), .pin8(1'b0), .pin9(1'b0), .pin10(1'b0),
    .pin11(OUT[7]), .pin12(OUT[6]), .pin13(OUT[5]), .pin14(OUT[4]), .pin15(OUT[3]), .pin16(OUT[2]),
    .pin17(OUT[1]), .pin18(OUT[0]), .pin19(IRO), .pin20(1'b1));
endmodule

/* Test case:
CLK INP CLR IRI IRO VAL INSTR OUT
C   20  0   0   1    20  1     Z
C   0   0   1   0    20  1     4
C   11  0   1   1    20  1     Z
C   239 0   0   1    239 14    Z    
*/
