// Digital circuit jkflopflop.dig as structural Verilog
module jkflopflop (
  input  CLK,
  input  J,
  input  K,
  output NQ,
  output Q
);

  wire and_1_out, and_2_out;

  and and_1 (and_1_out, J, CLK);
  and and_2 (and_2_out, CLK, K);
  srlatch srlatch_1 (.S(and_1_out), .R(and_2_out), .NQ(NQ), .Q(Q));
endmodule
