// Digital circuit mccount.dig as structural Verilog
module mccount (
  input  CLK,
  output [3:0] NUM
);

  wire _74138_1_pin7, _74138_1_pin9, _74138_1_pin11, _74138_1_pin12, _74138_1_pin13, _74138_1_pin14,
       _74138_1_pin15, _74163_1_pin1;

  _74163 _74163_1 (
    .pin1(_74163_1_pin1), .pin2(CLK), .pin3(1'b0), .pin4(1'b0), .pin5(1'b0), .pin6(1'b0), .pin7(1'b1),
    .pin8(1'b0), .pin9(1'b1), .pin10(1'b1), .pin11(NUM[3]), .pin12(NUM[2]), .pin13(NUM[1]), .pin14(NUM[0]),
    .pin16(1'b1));  // open: pin15
  LED led_1 (.in(NUM[3]));
  LED led_2 (.in(_74138_1_pin7));
  _74138 _74138_1 (
    .pin1(NUM[0]), .pin2(NUM[1]), .pin3(NUM[2]), .pin4(1'b0), .pin5(1'b0), .pin6(1'b1), .pin7(_74138_1_pin7),
    .pin8(1'b0), .pin9(_74138_1_pin9), .pin10(_74163_1_pin1), .pin11(_74138_1_pin11), .pin12(_74138_1_pin12),
    .pin13(_74138_1_pin13), .pin14(_74138_1_pin14), .pin15(_74138_1_pin15), .pin16(1'b1));
  LED led_3 (.in(_74138_1_pin15));
  LED led_4 (.in(_74138_1_pin14));
  LED led_5 (.in(_74138_1_pin13));
  LED led_6 (.in(_74138_1_pin12));
  LED led_7 (.in(_74138_1_pin11));
  LED led_8 (.in(_74163_1_pin1));
  LED led_9 (.in(_74138_1_pin9));
endmodule
