// Digital circuit memory.dig as structural Verilog
module memory (
  input  CS,
  input  WE,
  input  [7:0] DATA,
  input  [3:0] ADDR,
  output [7:0] OUT
);

  wire _7404_1_p9, _7404_1_p10, _7404_1_p11, _7404_1_p12, _7404_1_p13, _7404_1_p14, _7404_2_p9, _7404_2_p10,
       _7404_2_p11, _74189_1_p13, _74189_1_p14, _74189_1_p15, _74189_1_p16, _74189_2_p13, _74189_2_p14,
       _74189_2_p15, _74189_2_p16, and_1_out, not_1_out, not_2_out;

  // _74189 _74189_1: pin names not known; wires that end beside it: ADDR[0], ADDR[1], ADDR[2], ADDR[3], DATA[0], DATA[1], DATA[2], DATA[3], CS, WE, 1'b1, 1'b0, _74189_1_p13, _74189_1_p14, _74189_1_p15, _74189_1_p16
  // _74189 _74189_2: pin names not known; wires that end beside it: ADDR[0], ADDR[1], ADDR[2], ADDR[3], DATA[4], DATA[5], DATA[6], DATA[7], CS, WE, 1'b1, 1'b0, _74189_2_p13, _74189_2_p14, _74189_2_p15, _74189_2_p16
  // _7404 _7404_1: pin names not known; wires that end beside it: _74189_1_p13, _74189_1_p14, _74189_1_p15, _74189_1_p16, _74189_2_p13, _74189_2_p14, 1'b1, 1'b0, _7404_1_p9, _7404_1_p10, _7404_1_p11, _7404_1_p12, _7404_1_p13, _7404_1_p14
  // _7404 _7404_2: pin names not known; wires that end beside it: _74189_2_p15, _74189_2_p16, 1'b1, 1'b1, 1'b1, 1'b1, 1'b1, 1'b0, _7404_2_p9, _7404_2_p10, _7404_2_p11, 1'b0, _7404_2_p11, _7404_2_p11
  not not_1 (not_1_out, CS);
  and and_1 (and_1_out, not_1_out, WE);
  not not_2 (not_2_out, and_1_out);
  _74245 _74245_1 (
    .pin1(1'b1), .pin2(_7404_1_p9), .pin3(_7404_1_p10), .pin4(_7404_1_p11), .pin5(_7404_1_p12),
    .pin6(_7404_1_p13), .pin7(_7404_1_p14), .pin8(_7404_2_p9), .pin9(_7404_2_p10), .pin10(1'b0),
    .pin11(OUT[7]), .pin12(OUT[6]), .pin13(OUT[5]), .pin14(OUT[4]), .pin15(OUT[3]), .pin16(OUT[2]),
    .pin17(OUT[1]), .pin18(OUT[0]), .pin19(not_2_out), .pin20(1'b1));
endmodule
