// Digital circuit msjkflipflop.dig as structural Verilog
module msjkflipflop (
  input  CLK,
  input  J,
  input  K,
  output NQ,
  output Q
);

  wire and_1_out, and_2_out, and_3_out, and_4_out, not_1_out, srlatch_1_nq, srlatch_1_q;

  not not_1 (not_1_out, CLK);
  and and_1 (and_1_out, J, Q, CLK);
  and and_2 (and_2_out, CLK, NQ, K);
  srlatch srlatch_1 (.S(and_1_out), .R(and_2_out), .NQ(srlatch_1_nq), .Q(srlatch_1_q));
  and and_3 (and_3_out, srlatch_1_nq, not_1_out);
  and and_4 (and_4_out, srlatch_1_q, not_1_out);
  srlatch srlatch_2 (.S(and_3_out), .R(and_4_out), .NQ(NQ), .Q(Q));
endmodule
