// Digital circuit pc.dig as structural Verilog
module pc (
  input  CLK,
  input  CLR,
  input  INCR,
  input  PO,
  output [7:0] COUNTER
);

  wire and_1_out, not_1_out, not_2_out;
  wire [3:0] counter_1_out;

  not not_1 (not_1_out, INCR);
  and and_1 (and_1_out, not_1_out, CLK);
  not not_2 (not_2_out, and_1_out);
  counter counter_1 (.CLK(not_2_out), .CLR(CLR), .OUT(counter_1_out));
  _74245 _74245_1 (
    .pin1(1'b1), .pin2(counter_1_out[0]), .pin3(counter_1_out[1]), .pin4(counter_1_out[2]),
    .pin5(counter_1_out[3]), .pin6(1'b0), .pin7(1'b0), .pin8(1'b0), .pin9(1'b0), .pin10(1'b0),
    .pin11(COUNTER[7]), .pin12(COUNTER[6]), .pin13(COUNTER[5]), .pin14(COUNTER[4]), .pin15(COUNTER[3]),
    .pin16(COUNTER[2]), .pin17(COUNTER[1]), .pin18(COUNTER[0]), .pin19(PO), .pin20(1'b1));
endmodule
