// Digital circuit register.dig as structural Verilog
module register (
  input  CLK,
  input  [7:0] INP,
  input  SET,
  input  GET,
  output [7:0] OUT
);

  _74173 _74173_1 (
    .pin1(GET), .pin2(GET), .pin3(OUT[0]), .pin4(OUT[1]), .pin5(OUT[2]), .pin6(OUT[3]), .pin7(CLK),
    .pin8(1'b0), .pin9(SET), .pin10(SET), .pin11(INP[3]), .pin12(INP[2]), .pin13(INP[1]), .pin14(INP[0]),
    .pin15(1'b0), .pin16(1'b1));
  _74173 _74173_2 (
    .pin1(GET), .pin2(GET), .pin3(OUT[4]), .pin4(OUT[5]), .pin5(OUT[6]), .pin6(OUT[7]), .pin7(CLK),
    .pin8(1'b0), .pin9(SET), .pin10(SET), .pin11(INP[7]), .pin12(INP[6]), .pin13(INP[5]), .pin14(INP[4]),
    .pin15(1'b0), .pin16(1'b1));
endmodule
