// Digital circuit registerr.dig as structural Verilog
module registerr (
  input  CLK,
  input  [7:0] INP,
  input  SET,
  input  RST,
  input  GET,
  output [7:0] OUT,
  output [7:0] VAL
);

  _74173 _74173_1 (
    .pin1(1'b0), .pin2(1'b0), .pin3(VAL[0]), .pin4(VAL[1]), .pin5(VAL[2]), .pin6(VAL[3]), .pin7(CLK),
    .pin8(1'b0), .pin9(SET), .pin10(SET), .pin11(INP[3]), .pin12(INP[2]), .pin13(INP[1]), .pin14(INP[0]),
    .pin15(RST), .pin16(1'b1));
  _74173 _74173_2 (
    .pin1(1'b0), .pin2(1'b0), .pin3(VAL[4]), .pin4(VAL[5]), .pin5(VAL[6]), .pin6(VAL[7]), .pin7(CLK),
    .pin8(1'b0), .pin9(SET), .pin10(SET), .pin11(INP[7]), .pin12(INP[6]), .pin13(INP[5]), .pin14(INP[4]),
    .pin15(RST), .pin16(1'b1));
  _74245 _74245_1 (
    .pin1(1'b1), .pin2(VAL[0]), .pin3(VAL[1]), .pin4(VAL[2]), .pin5(VAL[3]), .pin6(VAL[4]), .pin7(VAL[5]),
    .pin8(VAL[6]), .pin9(VAL[7]), .pin10(1'b0), .pin11(OUT[7]), .pin12(OUT[6]), .pin13(OUT[5]),
    .pin14(OUT[4]), .pin15(OUT[3]), .pin16(OUT[2]), .pin17(OUT[1]), .pin18(OUT[0]), .pin19(GET), .pin20(1'b1));
endmodule

/* Test case:
CLK INP RST SET GET VAL  OUT
C   256 0   0   1   256  Z
C   255 0   1   0   256  256
C   254 1   1   1   0    Z
C   253 1   0   0   253  253
*/
